// Logisim project multiplexor.circ as structural Verilog: 1 circuit, main circuit main
module main (
  input  [7:0] in_1,
  input  [7:0] in_2,
  input  [7:0] in_3,
  input  [7:0] in_4,
  input  [7:0] in_5,
  input  [7:0] in_6,
  input  in_7,
  input  [7:0] in_8,
  input  [2:0] in_9,
  input  [7:0] in_10,
  output [7:0] out_11
);

  Multiplexer #(.select(3), .width(8)) multiplexer_1 (
    .in0(in_1), .in1(in_2), .in2(in_3), .in3(in_4), .in4(in_5), .in5(in_6), .in6(in_8), .in7(in_10),
    .out(out_11), .sel(in_9), .en(in_7));
endmodule
