// Logisim project Fibonacci JK.circ as structural Verilog: 1 circuit, main circuit FIBONACCI
module FIBONACCI (
  input  in_1
);

  wire and_1_out, and_2_out, and_3_out, and_4_out, and_5_out, clock_1_out, j_k_ff_1_q, j_k_ff_1_qn,
       j_k_ff_2_q, j_k_ff_3_q, j_k_ff_3_qn, j_k_ff_4_q, j_k_ff_4_qn, n7_segment_display_driver_1_p5,
       n7_segment_display_driver_1_p6, n7_segment_display_driver_1_p7, n7_segment_display_driver_1_p8,
       n7_segment_display_driver_1_p9, n7_segment_display_driver_1_p10, n7_segment_display_driver_1_p11,
       or_1_out, or_2_out;

  Clock clock_1 (.out(clock_1_out));
  and and_1 (and_1_out, j_k_ff_1_q, j_k_ff_4_q);
  and and_2 (and_2_out, j_k_ff_4_q, j_k_ff_3_qn);
  and and_3 (and_3_out, j_k_ff_4_q, j_k_ff_3_q);
  or or_1 (or_1_out, j_k_ff_1_q, j_k_ff_2_q);
  J_K_Flip_Flop j_k_ff_1 (
    .J(and_2_out), .clk(clock_1_out), .K(in_1), .Q(j_k_ff_1_q), .Qn(j_k_ff_1_qn));  // open: preset, en, reset
  J_K_Flip_Flop j_k_ff_2 (.J(and_3_out), .clk(clock_1_out), .K(in_1), .Q(j_k_ff_2_q));  // open: Qn, preset, en, reset
  J_K_Flip_Flop j_k_ff_3 (
    .J(and_1_out), .clk(clock_1_out), .K(j_k_ff_4_q), .Q(j_k_ff_3_q), .Qn(j_k_ff_3_qn));  // open: preset, en, reset
  J_K_Flip_Flop j_k_ff_4 (
    .J(j_k_ff_1_qn), .clk(clock_1_out), .K(or_1_out), .Q(j_k_ff_4_q), .Qn(j_k_ff_4_qn));  // open: preset, en, reset
  and and_4 (and_4_out, j_k_ff_1_q, j_k_ff_2_q);
  and and_5 (and_5_out, j_k_ff_4_qn, j_k_ff_1_q);
  or or_2 (or_2_out, and_4_out, and_5_out);
  // _7_segment_display_driver 7_segment_display_driver_1: pin names not known; wires that end beside it: or_2_out, j_k_ff_2_q, j_k_ff_3_q, j_k_ff_4_q, n7_segment_display_driver_1_p5, n7_segment_display_driver_1_p6, n7_segment_display_driver_1_p7, n7_segment_display_driver_1_p8, n7_segment_display_driver_1_p9, n7_segment_display_driver_1_p10, n7_segment_display_driver_1_p11
  _7_Segment_Display u_7_segment_display_1 (
    .g(n7_segment_display_driver_1_p11), .f(n7_segment_display_driver_1_p10),
    .a(n7_segment_display_driver_1_p5), .b(n7_segment_display_driver_1_p6),
    .e(n7_segment_display_driver_1_p9), .d(n7_segment_display_driver_1_p8), .c(n7_segment_display_driver_1_p7));  // open: dp

  // Notes on the sheet:
  //   Contador Fibonacci con Flip Flop JK 
  //   JA
  //   KA
  //   JB
  //   KB
  //   JC
  //   KC
  //   JD
  //   KD
  //   A
  //   B
  //   C
  //   D
  //   C
  //   A
  //   B
  //   D
endmodule
